// Logisim project ASM_Lesson10_Page4.circ as structural Verilog: 1 circuit, main circuit main
module main (
  input  GO,
  input  GO_2,
  input  EN,
  output Done,
  output Done_2
);

  wire and_1_out, and_2_out, and_3_out, and_4_out, CLK_out, d_ff_1_p5, d_ff_2_p5, d_ff_2_p6, d_ff_3_p5,
       d_ff_4_p5, d_ff_4_p6, or_1_out, or_2_out, xor_1_out, xor_2_out;

  Clock CLK (.out(CLK_out));
  and and_1 (and_1_out, d_ff_1_p5, d_ff_2_p6);
  and and_2 (and_2_out, d_ff_2_p6, GO);
  and and_3 (and_3_out, d_ff_3_p5, d_ff_4_p6);
  and and_4 (and_4_out, d_ff_4_p6, GO_2);
  // Probe on xor_1_out
  xor xor_1 (xor_1_out, d_ff_2_p5, d_ff_1_p5);
  // Probe on or_1_out
  or or_1 (or_1_out, and_1_out, and_2_out);
  // Probe on xor_2_out
  xor xor_2 (xor_2_out, d_ff_4_p5, d_ff_3_p5);
  // Probe on or_2_out
  or or_2 (or_2_out, and_3_out, and_4_out);
  // D_Flip_Flop d_ff_1: pin names not known; wires that end beside it: xor_1_out, CLK_out, 1'b1, 1'b1, d_ff_1_p5
  // D_Flip_Flop d_ff_2: pin names not known; wires that end beside it: or_1_out, CLK_out, 1'b1, 1'b1, d_ff_2_p5, d_ff_2_p6
  // D_Flip_Flop #(.trigger("high")) d_ff_3: pin names not known; wires that end beside it: xor_2_out, EN, 1'b1, 1'b1, d_ff_3_p5
  // D_Flip_Flop #(.trigger("high")) d_ff_4: pin names not known; wires that end beside it: or_2_out, EN, 1'b1, 1'b1, d_ff_4_p5, d_ff_4_p6
  and and_5 (Done, d_ff_1_p5, d_ff_2_p5);
  and and_6 (Done_2, d_ff_3_p5, d_ff_4_p5);

  // Notes on the sheet:
  //   #0
  //   #1
  //   #0
  //   #1
endmodule
