// Logisim project CombinatoryMSI.circ as structural Verilog: 1 circuit, main circuit main
module main (
  input  I0,
  input  I0_2,
  input  I0_3,
  input  I1,
  input  I1_2,
  input  I1_3,
  input  I2,
  input  I3,
  input  I2_2,
  input  I2_3,
  input  I4,
  input  I5,
  input  I3_2,
  input  I3_3,
  input  I6,
  input  I7,
  input  S0,
  input  S1,
  input  S0_2,
  input  S1_2,
  input  En,
  input  S0_3,
  input  S1_3,
  input  S2,
  input  S0_4,
  input  D,
  input  S0_5,
  input  S1_4,
  input  S1_5,
  input  S2_2,
  input  En_2,
  input  S0_6,
  input  S1_6,
  input  En_3,
  input  En_4,
  input  I0_4,
  input  I1_4,
  input  I2_4,
  input  I3_4,
  input  En_5
);

  wire and_1_out, and_2_out, and_3_out, and_4_out, and_5_out, and_6_out, and_7_out, and_8_out, and_9_out,
       and_10_out, and_11_out, and_12_out, and_13_out, and_14_out, and_15_out, and_16_out, and_17_out,
       and_18_out, and_19_out, and_20_out, and_21_out, and_22_out, decoder_1_out0, decoder_1_out1,
       decoder_2_out0, decoder_2_out1, decoder_2_out2, decoder_2_out3, decoder_3_out0, decoder_3_out1,
       decoder_3_out2, decoder_3_out3, multiplexer_1_out, multiplexer_2_out, multiplexer_3_out, or_1_out,
       or_2_out, or_3_out, or_4_out, or_5_out;

  and and_1 (and_1_out, I0_4, ~I1_4);  // AND_Gate
  or or_1 (or_1_out, ~I2_4, ~I3_4);  // OR_Gate
  and and_2 (and_2_out, I0, ~S0, ~S1);  // AND_Gate
  and and_3 (and_3_out, I1_2, S0, ~S1);  // AND_Gate
  and and_4 (and_4_out, I2_2, ~S0, S1);  // AND_Gate
  and and_5 (and_5_out, I3_2, S0, S1);
  and and_6 (and_6_out, D, ~S0_6, ~S1_6, ~En_3);  // AND_Gate
  and and_7 (and_7_out, D, S0_6, ~S1_6, ~En_3);  // AND_Gate
  and and_8 (and_8_out, D, ~S0_6, S1_6, ~En_3);  // AND_Gate
  and and_9 (and_9_out, D, S0_6, S1_6, ~En_3);  // AND_Gate
  and and_10 (and_10_out, I0_4, I2_4, ~I3_4);  // AND_Gate
  or or_2 (or_2_out, ~I0_4, ~I1_4, ~I2_4, ~I3_4);  // OR_Gate
  LED O0 (.in(and_6_out));
  LED O1 (.in(and_7_out));
  LED O2 (.in(and_8_out));
  LED O3 (.in(and_9_out));
  or or_3 (or_3_out, and_1_out, and_10_out);
  and and_11 (and_11_out, or_1_out, I0_4, I1_4);
  // Probe on nothing
  or or_4 (or_4_out, and_2_out, and_3_out, and_4_out, and_5_out);
  and and_12 (and_12_out, or_3_out, ~En_5);  // AND_Gate
  and and_13 (and_13_out, and_11_out, ~En_5);  // AND_Gate
  and and_14 (and_14_out, or_2_out, ~En_5);  // AND_Gate
  LED Y (.in(or_4_out));
  LED O0_2 (.in(and_12_out));
  LED O1_2 (.in(and_13_out));
  LED GS (.in(and_14_out));
  and and_15 (and_15_out, ~S0_5, ~S1_5, ~En_4);  // AND_Gate
  and and_16 (and_16_out, S0_5, ~S1_5, ~En_4);  // AND_Gate
  and and_17 (and_17_out, ~S0_5, S1_5, ~En_4);  // AND_Gate
  and and_18 (and_18_out, S0_5, S1_5, ~En_4);  // AND_Gate
  and and_19 (and_19_out, I0_2, ~S0_2, ~S1_2, En);  // AND_Gate
  and and_20 (and_20_out, I1_3, S0_2, ~S1_2, En);  // AND_Gate
  and and_21 (and_21_out, I2_3, ~S0_2, S1_2, En);  // AND_Gate
  and and_22 (and_22_out, I3_3, S0_2, S1_2, En);
  LED O0_3 (.in(and_15_out));
  LED O1_3 (.in(and_16_out));
  LED O2_2 (.in(and_17_out));
  LED O3_2 (.in(and_18_out));
  or or_5 (or_5_out, and_19_out, and_20_out, and_21_out, and_22_out);
  LED Y_2 (.in(or_5_out));
  Decoder #(.select(2), .disabled(0)) decoder_1 (
    .out0(decoder_1_out0), .out1(decoder_1_out1), .sel({1'b0, S2_2}), .en(En_2));  // open: out2, out3
  Multiplexer #(.select(2), .disabled(0), .enable("false")) multiplexer_1 (
    .in0(I0_3), .in1(I1), .in2(I2), .in3(I3), .out(multiplexer_1_out), .sel({S1_3, S0_3}));
  Multiplexer #(.select(2), .disabled(0), .enable("false")) multiplexer_2 (
    .in0(I4), .in1(I5), .in2(I6), .in3(I7), .out(multiplexer_2_out), .sel({S1_3, S0_3}));
  Decoder #(.select(2), .disabled(0)) decoder_2 (
    .out0(decoder_2_out0), .out1(decoder_2_out1), .out2(decoder_2_out2), .out3(decoder_2_out3),
    .sel({S1_4, S0_4}), .en(decoder_1_out0));
  Decoder #(.select(2), .disabled(0)) decoder_3 (
    .out0(decoder_3_out0), .out1(decoder_3_out1), .out2(decoder_3_out2), .out3(decoder_3_out3),
    .sel({S1_4, S0_4}), .en(decoder_1_out1));
  Multiplexer #(.select(2), .disabled(0), .enable("false")) multiplexer_3 (
    .in0(multiplexer_1_out), .in1(multiplexer_1_out), .in2(multiplexer_2_out), .in3(multiplexer_2_out),
    .out(multiplexer_3_out), .sel({S2, 1'b0}));
  LED O0_4 (.in(decoder_2_out0));
  LED O1_4 (.in(decoder_2_out1));
  LED O2_3 (.in(decoder_2_out2));
  LED O3_3 (.in(decoder_2_out3));
  LED O4 (.in(decoder_3_out0));
  LED O5 (.in(decoder_3_out1));
  LED O6 (.in(decoder_3_out2));
  LED O7 (.in(decoder_3_out3));
  LED Y_3 (.in(multiplexer_3_out));
  // Probe on nothing

  // Notes on the sheet:
  //   MUX4x1
  //   DEMUX1x4 | En active low
  //   PENC 4 ints | Highest Prio -> 0 | In active low | En active low
  //   DEC 2 bits | En active low
  //   MUX4x1 | En active high
  //   DEC 3 bits | En active high
  //   MUX8x1
endmodule
